// Logisim project Calculatrice.circ as structural Verilog: 5 circuits, main circuit main
module main (
  input  in_1,
  input  _8,
  input  _8_2,
  input  _4,
  input  _4_2,
  input  _2,
  input  _2_2,
  input  _1,
  input  _1_2,
  input  _8_3,
  input  _8_4,
  input  _4_3,
  input  _4_4,
  input  _2_3,
  input  _2_4,
  input  _1_3,
  input  _1_4,
  input  _8_5,
  input  _8_6,
  input  _4_5,
  input  _4_6,
  input  _2_5,
  input  _2_6,
  input  _1_5,
  input  _1_6,
  input  _8_7,
  input  _8_8,
  input  _4_7,
  input  _4_8,
  input  _2_7,
  input  _2_8,
  input  _1_7,
  input  _1_8,
  input  in_34
);

  wire additioneur_1_retenue_2, additioneur_1_somme, additioneur_2_retenue_2, additioneur_2_somme,
       additioneur_3_retenue_2, additioneur_3_somme, additioneur_4_retenue_2, additioneur_4_somme,
       additioneur_5_retenue_2, additioneur_5_somme, additioneur_6_retenue_2, additioneur_6_somme,
       additioneur_7_retenue_2, additioneur_7_somme, additioneur_8_retenue_2, additioneur_8_somme,
       additioneur_9_retenue_2, additioneur_9_somme, additioneur_10_retenue_2, additioneur_10_somme,
       additioneur_11_retenue_2, additioneur_11_somme, additioneur_12_retenue_2, additioneur_12_somme,
       additioneur_13_retenue_2, additioneur_13_somme, additioneur_14_retenue_2, additioneur_14_somme,
       additioneur_15_retenue_2, additioneur_15_somme, additioneur_16_retenue_2, additioneur_16_somme,
       affichage_1_a, affichage_1_b, affichage_1_c, affichage_1_d, affichage_1_e, affichage_1_f,
       affichage_1_g, affichage_2_a, affichage_2_b, affichage_2_c, affichage_2_d, affichage_2_e,
       affichage_2_f, affichage_2_g, affichage_3_a, affichage_3_b, affichage_3_c, affichage_3_d,
       affichage_3_e, affichage_3_f, affichage_3_g, affichage_4_a, affichage_4_b, affichage_4_c,
       affichage_4_d, affichage_4_e, affichage_4_f, affichage_4_g, affichage_5_a, affichage_5_b,
       affichage_5_c, affichage_5_d, affichage_5_e, affichage_5_f, affichage_5_g, affichage_6_a,
       affichage_6_b, affichage_6_c, affichage_6_d, affichage_6_e, affichage_6_f, affichage_6_g,
       affichage_7_a, affichage_7_b, affichage_7_c, affichage_7_d, affichage_7_e, affichage_7_f,
       affichage_7_g, affichage_8_a, affichage_8_b, affichage_8_c, affichage_8_d, affichage_8_e,
       affichage_8_f, affichage_8_g, affichage_9_a, affichage_9_b, affichage_9_c, affichage_9_d,
       affichage_9_e, affichage_9_f, affichage_9_g, affichage_10_a, affichage_10_b, affichage_10_c,
       affichage_10_d, affichage_10_e, affichage_10_f, affichage_10_g, affichage_11_a, affichage_11_b,
       affichage_11_c, affichage_11_d, affichage_11_e, affichage_11_f, affichage_11_g, affichage_12_a,
       affichage_12_b, affichage_12_c, affichage_12_d, affichage_12_e, affichage_12_f, affichage_12_g,
       affichage_13_a, affichage_13_b, affichage_13_c, affichage_13_d, affichage_13_e, affichage_13_f,
       affichage_13_g, not_1_out, retenuedecimale_1__1_2, retenuedecimale_1__2_2, retenuedecimale_1__4_2,
       retenuedecimale_1__8_2, retenuedecimale_1_retenue_2, retenuedecimale_2__1_2, retenuedecimale_2__2_2,
       retenuedecimale_2__4_2, retenuedecimale_2__8_2, retenuedecimale_2_retenue_2, retenuedecimale_3__1_2,
       retenuedecimale_3__2_2, retenuedecimale_3__4_2, retenuedecimale_3__8_2, retenuedecimale_3_retenue_2,
       retenuedecimale_4__1_2, retenuedecimale_4__2_2, retenuedecimale_4__4_2, retenuedecimale_4__8_2,
       retenuedecimale_4_retenue_2;

  affichage affichage_1 (
    .in_1(_8_2), .in_2(_4_2), .in_3(_2_2), .in_4(_1_2), .a(affichage_1_a), .b(affichage_1_b),
    .c(affichage_1_c), .d(affichage_1_d), .e(affichage_1_e), .f(affichage_1_f), .g(affichage_1_g));
  affichage affichage_2 (
    .in_1(_8_4), .in_2(_4_4), .in_3(_2_4), .in_4(_1_4), .a(affichage_2_a), .b(affichage_2_b),
    .c(affichage_2_c), .d(affichage_2_d), .e(affichage_2_e), .f(affichage_2_f), .g(affichage_2_g));
  affichage affichage_3 (
    .in_1(_8_6), .in_2(_4_6), .in_3(_2_6), .in_4(_1_6), .a(affichage_3_a), .b(affichage_3_b),
    .c(affichage_3_c), .d(affichage_3_d), .e(affichage_3_e), .f(affichage_3_f), .g(affichage_3_g));
  affichage affichage_4 (
    .in_1(_8_8), .in_2(_4_8), .in_3(_2_8), .in_4(_1_8), .a(affichage_4_a), .b(affichage_4_b),
    .c(affichage_4_c), .d(affichage_4_d), .e(affichage_4_e), .f(affichage_4_f), .g(affichage_4_g));
  _7_Segment_Display u_7_segment_display_1 (
    .g(affichage_1_g), .f(affichage_1_f), .a(affichage_1_a), .b(affichage_1_b), .e(affichage_1_e),
    .d(affichage_1_d), .c(affichage_1_c));  // open: dp
  additioneur additioneur_1 (
    .soustraction(in_1), .A(_1_2), .retenue(retenuedecimale_2_retenue_2), .B(_1),
    .somme(additioneur_1_somme), .retenue_2(additioneur_1_retenue_2));
  _7_Segment_Display u_7_segment_display_2 (
    .g(affichage_2_g), .f(affichage_2_f), .a(affichage_2_a), .b(affichage_2_b), .e(affichage_2_e),
    .d(affichage_2_d), .c(affichage_2_c));  // open: dp
  additioneur additioneur_2 (
    .soustraction(in_1), .A(_1_4), .retenue(retenuedecimale_3_retenue_2), .B(_1_3),
    .somme(additioneur_2_somme), .retenue_2(additioneur_2_retenue_2));
  _7_Segment_Display u_7_segment_display_3 (
    .g(affichage_3_g), .f(affichage_3_f), .a(affichage_3_a), .b(affichage_3_b), .e(affichage_3_e),
    .d(affichage_3_d), .c(affichage_3_c));  // open: dp
  _7_Segment_Display u_7_segment_display_4 (
    .g(affichage_4_g), .f(affichage_4_f), .a(affichage_4_a), .b(affichage_4_b), .e(affichage_4_e),
    .d(affichage_4_d), .c(affichage_4_c));  // open: dp
  additioneur additioneur_3 (
    .soustraction(in_1), .A(_2_2), .retenue(additioneur_1_retenue_2), .B(_2), .somme(additioneur_3_somme),
    .retenue_2(additioneur_3_retenue_2));
  additioneur additioneur_4 (
    .soustraction(in_1), .A(_2_4), .retenue(additioneur_2_retenue_2), .B(_2_3), .somme(additioneur_4_somme),
    .retenue_2(additioneur_4_retenue_2));
  additioneur additioneur_5 (
    .soustraction(in_1), .A(_1_6), .retenue(retenuedecimale_4_retenue_2), .B(_1_5),
    .somme(additioneur_5_somme), .retenue_2(additioneur_5_retenue_2));
  additioneur additioneur_6 (
    .soustraction(in_1), .A(_1_8), .retenue(in_34), .B(_1_7), .somme(additioneur_6_somme),
    .retenue_2(additioneur_6_retenue_2));
  additioneur additioneur_7 (
    .soustraction(in_1), .A(_4_2), .retenue(additioneur_3_retenue_2), .B(_4), .somme(additioneur_7_somme),
    .retenue_2(additioneur_7_retenue_2));
  additioneur additioneur_8 (
    .soustraction(in_1), .A(_4_4), .retenue(additioneur_4_retenue_2), .B(_4_3), .somme(additioneur_8_somme),
    .retenue_2(additioneur_8_retenue_2));
  additioneur additioneur_9 (
    .soustraction(in_1), .A(_2_6), .retenue(additioneur_5_retenue_2), .B(_2_5), .somme(additioneur_9_somme),
    .retenue_2(additioneur_9_retenue_2));
  additioneur additioneur_10 (
    .soustraction(in_1), .A(_2_8), .retenue(additioneur_6_retenue_2), .B(_2_7), .somme(additioneur_10_somme),
    .retenue_2(additioneur_10_retenue_2));
  additioneur additioneur_11 (
    .soustraction(in_1), .A(_8_2), .retenue(additioneur_7_retenue_2), .B(_8), .somme(additioneur_11_somme),
    .retenue_2(additioneur_11_retenue_2));
  additioneur additioneur_12 (
    .soustraction(in_1), .A(_8_4), .retenue(additioneur_8_retenue_2), .B(_8_3), .somme(additioneur_12_somme),
    .retenue_2(additioneur_12_retenue_2));
  additioneur additioneur_13 (
    .soustraction(in_1), .A(_4_6), .retenue(additioneur_9_retenue_2), .B(_4_5), .somme(additioneur_13_somme),
    .retenue_2(additioneur_13_retenue_2));
  additioneur additioneur_14 (
    .soustraction(in_1), .A(_4_8), .retenue(additioneur_10_retenue_2), .B(_4_7),
    .somme(additioneur_14_somme), .retenue_2(additioneur_14_retenue_2));
  retenueDecimale retenuedecimale_1 (
    .retenue_2(retenuedecimale_1_retenue_2), ._8_2(retenuedecimale_1__8_2), ._4_2(retenuedecimale_1__4_2),
    ._2_2(retenuedecimale_1__2_2), ._1_2(retenuedecimale_1__1_2), .soustration(in_1),
    .retenue(additioneur_11_retenue_2), ._8(additioneur_11_somme), ._4(additioneur_7_somme),
    ._2(additioneur_3_somme), ._1(additioneur_1_somme));
  additioneur additioneur_15 (
    .soustraction(in_1), .A(_8_6), .retenue(additioneur_13_retenue_2), .B(_8_5),
    .somme(additioneur_15_somme), .retenue_2(additioneur_15_retenue_2));
  additioneur additioneur_16 (
    .soustraction(in_1), .A(_8_8), .retenue(additioneur_14_retenue_2), .B(_8_7),
    .somme(additioneur_16_somme), .retenue_2(additioneur_16_retenue_2));
  retenueDecimale retenuedecimale_2 (
    .retenue_2(retenuedecimale_2_retenue_2), ._8_2(retenuedecimale_2__8_2), ._4_2(retenuedecimale_2__4_2),
    ._2_2(retenuedecimale_2__2_2), ._1_2(retenuedecimale_2__1_2), .soustration(in_1),
    .retenue(additioneur_12_retenue_2), ._8(additioneur_12_somme), ._4(additioneur_8_somme),
    ._2(additioneur_4_somme), ._1(additioneur_2_somme));
  retenueDecimale retenuedecimale_3 (
    .retenue_2(retenuedecimale_3_retenue_2), ._8_2(retenuedecimale_3__8_2), ._4_2(retenuedecimale_3__4_2),
    ._2_2(retenuedecimale_3__2_2), ._1_2(retenuedecimale_3__1_2), .soustration(in_1),
    .retenue(additioneur_15_retenue_2), ._8(additioneur_15_somme), ._4(additioneur_13_somme),
    ._2(additioneur_9_somme), ._1(additioneur_5_somme));
  retenueDecimale retenuedecimale_4 (
    .retenue_2(retenuedecimale_4_retenue_2), ._8_2(retenuedecimale_4__8_2), ._4_2(retenuedecimale_4__4_2),
    ._2_2(retenuedecimale_4__2_2), ._1_2(retenuedecimale_4__1_2), .soustration(in_1),
    .retenue(additioneur_16_retenue_2), ._8(additioneur_16_somme), ._4(additioneur_14_somme),
    ._2(additioneur_10_somme), ._1(additioneur_6_somme));
  affichage affichage_5 (
    .in_1(_8), .in_2(_4), .in_3(_2), .in_4(_1), .a(affichage_5_a), .b(affichage_5_b), .c(affichage_5_c),
    .d(affichage_5_d), .e(affichage_5_e), .f(affichage_5_f), .g(affichage_5_g));
  affichage affichage_6 (
    .in_1(_8_3), .in_2(_4_3), .in_3(_2_3), .in_4(_1_3), .a(affichage_6_a), .b(affichage_6_b),
    .c(affichage_6_c), .d(affichage_6_d), .e(affichage_6_e), .f(affichage_6_f), .g(affichage_6_g));
  affichage affichage_7 (
    .in_1(_8_5), .in_2(_4_5), .in_3(_2_5), .in_4(_1_5), .a(affichage_7_a), .b(affichage_7_b),
    .c(affichage_7_c), .d(affichage_7_d), .e(affichage_7_e), .f(affichage_7_f), .g(affichage_7_g));
  affichage affichage_8 (
    .in_1(_8_7), .in_2(_4_7), .in_3(_2_7), .in_4(_1_7), .a(affichage_8_a), .b(affichage_8_b),
    .c(affichage_8_c), .d(affichage_8_d), .e(affichage_8_e), .f(affichage_8_f), .g(affichage_8_g));
  _7_Segment_Display u_7_segment_display_5 (
    .g(affichage_5_g), .f(affichage_5_f), .a(affichage_5_a), .b(affichage_5_b), .e(affichage_5_e),
    .d(affichage_5_d), .c(affichage_5_c));  // open: dp
  _7_Segment_Display u_7_segment_display_6 (
    .g(affichage_6_g), .f(affichage_6_f), .a(affichage_6_a), .b(affichage_6_b), .e(affichage_6_e),
    .d(affichage_6_d), .c(affichage_6_c));  // open: dp
  _7_Segment_Display u_7_segment_display_7 (
    .g(affichage_7_g), .f(affichage_7_f), .a(affichage_7_a), .b(affichage_7_b), .e(affichage_7_e),
    .d(affichage_7_d), .c(affichage_7_c));  // open: dp
  _7_Segment_Display u_7_segment_display_8 (
    .g(affichage_8_g), .f(affichage_8_f), .a(affichage_8_a), .b(affichage_8_b), .e(affichage_8_e),
    .d(affichage_8_d), .c(affichage_8_c));  // open: dp
  not not_1 (not_1_out, 1'b1);
  affichage affichage_9 (
    .in_1(not_1_out), .in_2(not_1_out), .in_3(not_1_out), .in_4(retenuedecimale_1_retenue_2),
    .a(affichage_9_a), .b(affichage_9_b), .c(affichage_9_c), .d(affichage_9_d), .e(affichage_9_e),
    .f(affichage_9_f), .g(affichage_9_g));
  _7_Segment_Display u_7_segment_display_9 (
    .g(affichage_9_g), .f(affichage_9_f), .a(affichage_9_a), .b(affichage_9_b), .e(affichage_9_e),
    .d(affichage_9_d), .c(affichage_9_c));  // open: dp
  affichage affichage_10 (
    .in_1(retenuedecimale_1__8_2), .in_2(retenuedecimale_1__4_2), .in_3(retenuedecimale_1__2_2),
    .in_4(retenuedecimale_1__1_2), .a(affichage_10_a), .b(affichage_10_b), .c(affichage_10_c),
    .d(affichage_10_d), .e(affichage_10_e), .f(affichage_10_f), .g(affichage_10_g));
  _7_Segment_Display u_7_segment_display_10 (
    .g(affichage_10_g), .f(affichage_10_f), .a(affichage_10_a), .b(affichage_10_b), .e(affichage_10_e),
    .d(affichage_10_d), .c(affichage_10_c));  // open: dp
  affichage affichage_11 (
    .in_1(retenuedecimale_2__8_2), .in_2(retenuedecimale_2__4_2), .in_3(retenuedecimale_2__2_2),
    .in_4(retenuedecimale_2__1_2), .a(affichage_11_a), .b(affichage_11_b), .c(affichage_11_c),
    .d(affichage_11_d), .e(affichage_11_e), .f(affichage_11_f), .g(affichage_11_g));
  _7_Segment_Display u_7_segment_display_11 (
    .g(affichage_11_g), .f(affichage_11_f), .a(affichage_11_a), .b(affichage_11_b), .e(affichage_11_e),
    .d(affichage_11_d), .c(affichage_11_c));  // open: dp
  affichage affichage_12 (
    .in_1(retenuedecimale_3__8_2), .in_2(retenuedecimale_3__4_2), .in_3(retenuedecimale_3__2_2),
    .in_4(retenuedecimale_3__1_2), .a(affichage_12_a), .b(affichage_12_b), .c(affichage_12_c),
    .d(affichage_12_d), .e(affichage_12_e), .f(affichage_12_f), .g(affichage_12_g));
  _7_Segment_Display u_7_segment_display_12 (
    .g(affichage_12_g), .f(affichage_12_f), .a(affichage_12_a), .b(affichage_12_b), .e(affichage_12_e),
    .d(affichage_12_d), .c(affichage_12_c));  // open: dp
  affichage affichage_13 (
    .in_1(retenuedecimale_4__8_2), .in_2(retenuedecimale_4__4_2), .in_3(retenuedecimale_4__2_2),
    .in_4(retenuedecimale_4__1_2), .a(affichage_13_a), .b(affichage_13_b), .c(affichage_13_c),
    .d(affichage_13_d), .e(affichage_13_e), .f(affichage_13_f), .g(affichage_13_g));
  _7_Segment_Display u_7_segment_display_13 (
    .g(affichage_13_g), .f(affichage_13_f), .a(affichage_13_a), .b(affichage_13_b), .e(affichage_13_e),
    .d(affichage_13_d), .c(affichage_13_c));  // open: dp

  // Notes on the sheet:
  //   Activer la soustraction
endmodule

module affichage (
  input  in_1,
  input  in_2,
  input  in_3,
  input  in_4,
  output a,
  output b,
  output c,
  output d,
  output e,
  output f,
  output g
);

  wire and_1_out, and_2_out, and_3_out, and_4_out, and_5_out, and_6_out, and_7_out, and_8_out, and_9_out,
       and_10_out, and_11_out, and_12_out, and_13_out, not_1_out, not_2_out, not_3_out, not_4_out, not_5_out,
       not_6_out, or_1_out, or_2_out, or_3_out, or_4_out, or_5_out, or_6_out, or_7_out, or_8_out, or_9_out,
       or_10_out, or_11_out, or_12_out, or_13_out, or_14_out, or_15_out, or_16_out, xnor_1_out, xnor_2_out,
       xor_1_out;

  not not_1 (not_1_out, in_1);
  not not_2 (not_2_out, in_2);
  not not_3 (not_3_out, in_3);
  not not_4 (not_4_out, in_4);
  and and_1 (and_1_out, in_1, in_2);
  and and_2 (and_2_out, in_1, in_3);
  xnor xnor_1 (xnor_1_out, in_4, in_2);
  or or_1 (or_1_out, in_1, in_3);
  xnor xnor_2 (xnor_2_out, in_4, in_3);
  or or_2 (or_2_out, in_4, in_2);
  and and_3 (and_3_out, not_4_out, not_2_out);
  and and_4 (and_4_out, in_3, not_2_out);
  and and_5 (and_5_out, not_4_out, in_3);
  and and_6 (and_6_out, in_4, in_2);
  and and_7 (and_7_out, not_4_out, not_2_out);
  and and_8 (and_8_out, not_4_out, in_3);
  and and_9 (and_9_out, not_4_out, not_3_out);
  and and_10 (and_10_out, not_4_out, in_2);
  and and_11 (and_11_out, not_3_out, in_2);
  and and_12 (and_12_out, in_2, not_4_out);
  or or_3 (or_3_out, and_1_out, and_2_out);
  or or_4 (or_4_out, xnor_1_out, or_1_out);
  or or_5 (or_5_out, xnor_2_out, not_2_out);
  or or_6 (or_6_out, or_2_out, not_3_out);
  or or_7 (or_7_out, and_3_out, and_4_out);
  or or_8 (or_8_out, and_5_out, in_1);
  and and_13 (and_13_out, and_6_out, not_3_out);
  or or_9 (or_9_out, in_1, and_9_out, and_9_out);
  or or_10 (or_10_out, and_10_out, and_11_out);
  or or_11 (or_11_out, in_1, and_12_out);
  xor xor_1 (xor_1_out, in_3, in_2);
  or or_12 (or_12_out, or_7_out, or_8_out);
  or or_13 (or_13_out, and_7_out, and_8_out);
  or or_14 (or_14_out, or_9_out, or_10_out);
  or or_15 (or_15_out, or_11_out, xor_1_out);
  or or_16 (or_16_out, or_12_out, and_13_out);
  not not_5 (not_5_out, or_3_out);
  not not_6 (not_6_out, or_3_out);
  or or_17 (a, or_3_out, or_4_out);
  and and_14 (b, not_5_out, or_5_out);
  and and_15 (c, not_6_out, or_6_out);
  or or_18 (d, or_3_out, or_16_out);
  or or_19 (e, or_3_out, or_13_out);
  or or_20 (f, or_3_out, or_14_out);
  or or_21 (g, or_3_out, or_15_out);
endmodule

module additioneur (
  input  A,
  input  B,
  input  retenue,
  input  soustraction,
  output somme,
  output retenue_2
);

  wire demi_additionneur_1_out_4, demi_additionneur_1_out_5, demi_additionneur_2_out_5;

  demi_additionneur demi_additionneur_1 (
    .A(A), .out_4(demi_additionneur_1_out_4), .B(B), .out_5(demi_additionneur_1_out_5),
    .soustraction(soustraction));
  demi_additionneur demi_additionneur_2 (
    .A(demi_additionneur_1_out_4), .out_4(somme), .B(retenue), .out_5(demi_additionneur_2_out_5),
    .soustraction(soustraction));
  or or_1 (retenue_2, demi_additionneur_1_out_5, demi_additionneur_2_out_5);
endmodule

module retenueDecimale (
  input  soustration,
  input  retenue,
  input  _8,
  input  _4,
  input  _2,
  input  _1,
  output retenue_2,
  output _8_2,
  output _4_2,
  output _2_2,
  output _1_2
);

  wire additioneur_1_retenue_2, additioneur_1_somme, additioneur_2_retenue_2, additioneur_2_somme,
       additioneur_3_retenue_2, additioneur_3_somme, additioneur_4_somme, and_1_out, and_2_out, and_3_out,
       and_4_out, and_5_out, and_6_out, and_7_out, and_8_out, and_9_out, and_10_out, not_1_out, not_2_out,
       not_3_out, not_4_out, not_5_out, or_1_out;

  not not_1 (not_1_out, 1'b1);
  additioneur additioneur_1 (
    .soustraction(soustration), .A(_1), .retenue(not_1_out), .B(not_1_out), .somme(additioneur_1_somme),
    .retenue_2(additioneur_1_retenue_2));
  and and_1 (and_1_out, _8, _4);
  and and_2 (and_2_out, _8, _8, _2, _2);
  additioneur additioneur_2 (
    .soustraction(soustration), .A(_2), .retenue(additioneur_1_retenue_2), .B(1'b1),
    .somme(additioneur_2_somme), .retenue_2(additioneur_2_retenue_2));
  or or_1 (or_1_out, and_1_out, and_2_out);
  additioneur additioneur_3 (
    .soustraction(soustration), .A(_4), .retenue(additioneur_2_retenue_2), .B(1'b1),
    .somme(additioneur_3_somme), .retenue_2(additioneur_3_retenue_2));
  additioneur additioneur_4 (
    .soustraction(soustration), .A(_8), .retenue(additioneur_3_retenue_2), .B(not_1_out),
    .somme(additioneur_4_somme));  // open: retenue_2
  or or_2 (retenue_2, or_1_out, or_1_out, retenue, retenue);
  and and_3 (and_3_out, retenue_2, additioneur_4_somme);
  and and_4 (and_4_out, retenue_2, additioneur_3_somme);
  and and_5 (and_5_out, retenue_2, additioneur_2_somme);
  and and_6 (and_6_out, retenue_2, additioneur_1_somme);
  not not_2 (not_2_out, retenue_2);
  not not_3 (not_3_out, retenue_2);
  not not_4 (not_4_out, retenue_2);
  not not_5 (not_5_out, retenue_2);
  and and_7 (and_7_out, not_2_out, _1);
  and and_8 (and_8_out, _2, not_3_out);
  and and_9 (and_9_out, not_4_out, _4);
  and and_10 (and_10_out, not_5_out, _8);
  or or_3 (_8_2, and_3_out, and_10_out);
  or or_4 (_4_2, and_4_out, and_9_out);
  or or_5 (_2_2, and_5_out, and_8_out);
  or or_6 (_1_2, and_6_out, and_7_out);
endmodule

module demi_additionneur (
  input  A,
  input  B,
  input  soustraction,
  output out_4,
  output out_5
);

  wire xor_1_out;

  xor xor_1 (xor_1_out, A, soustraction);
  xor xor_2 (out_4, A, B);
  and and_1 (out_5, B, xor_1_out);
endmodule
